# Fritzing sketch PS (saved by Fritzing 0.9.3b)
breadboards: 1

parts:
  Part1 = Arduino Uno (Rev3)
  R1 = Resistor [tolerance=±5% resistance=1k package=THT]
  R2 = Resistor [tolerance=±5% resistance=220 package=THT]
  S3 = Pushbutton [package=THT]
  LED2 = LED - 5mm [color="Red (633nm)" package="5 mm [THT]"]
  7_Segment1 = 7 Segment Display
  T1 = LM35 Temperature Sensor [package="TO92 [THT]"]
  R3 = Resistor [tolerance=±5% resistance=500 package=THT]
  R4 = Resistor [tolerance=±5% resistance=500 package=THT]
  R5 = Resistor [tolerance=±5% resistance=500 package=THT]
  R6 = Resistor [tolerance=±5% resistance=500 package=THT]
  R7 = Resistor [tolerance=±5% resistance=500 package=THT]
  R8 = Resistor [tolerance=±5% resistance=500 package=THT]
  R9 = Resistor [tolerance=±5% resistance=500 package=THT]
  R10 = Resistor [tolerance=±5% resistance=500 package=THT]

nets:
  N1: Part1.A0, T1.Vout
  N2: Part1.D8, R10.Pin_1
  N3: Part1.D9_PWM, R9.Pin_1
  N4: Part1.D10_PWM/SS, R6.Pin_1
  N5: Part1.D11_PWM/MOSI, R5.Pin_1
  N6: Part1.D12/MISO, R4.Pin_0
  N7: Part1.D13/SCK, R3.Pin_1
  GND: Part1.GND, R2.Pin_0, S3.leg0, 7_Segment1.common_cathode, T1.GND
  N8: Part1.D4, R1.Pin_1, S3.leg1
  N9: Part1.D5_PWM, LED2.anode
  N10: Part1.D6_PWM, R8.Pin_1
  N11: Part1.D7, R7.Pin_1
  N12: Part1.5V, R1.Pin_0, T1.+Vs
  N13: R2.Pin_1, LED2.cathode
  N14: 7_Segment1.Segment_A#1, R7.Pin_0
  N15: 7_Segment1.Segment_F, R10.Pin_0
  N16: 7_Segment1.Segment_E, R9.Pin_0
  N17: 7_Segment1.Segment_D, R6.Pin_0
  N18: 7_Segment1.Segment_DP, R8.Pin_0
  N19: 7_Segment1.Segment_C, R5.Pin_0
  N20: 7_Segment1.Segment_B, R4.Pin_1
  N21: 7_Segment1.Segment_A#10, R3.Pin_0
